# Fritzing sketch d2t2 (saved by Fritzing 0.9.3b)
breadboards: 1

parts:
  Part1 = Adafruit T-Cobbler Plus [part_number="Adafruit #1989 and #2028"]
  LED1 = LED - 5mm [color="Red (633nm)" package="5 mm [THT]"]
  R1 = Resistor [tolerance=±5% resistance=56 package=THT]
  S1 = Pushbutton [package="[THT]"]
  R2 = Resistor [tolerance=±5% resistance=10k package=THT]
  J1 = Infrared Proximity Sensor

nets:
  N1: Part1.GPIO4, LED1.anode
  GND: Part1.GND, R1.Pin_0, R2.Pin_0, J1.GND
  N2: Part1.GPIO5, S1.Pin_3, S1.Pin_4, R2.Pin_1
  N3: Part1.GPIO6, J1.Vout
  +5V: Part1.+5V, S1.Pin_1, S1.Pin_2, J1.Vcc
  N4: LED1.cathode, R1.Pin_1

custom parts:
  Adafruit T-Cobbler Plus: The Raspberry Pi has landed on the Maker World like a 40-GPIO pinned, quad-USB ported, credit card sized bomb of DIY joy. And while you can use most of our great Model B accessories by hooking up our downgrade cable, its probably a good time to upgrade your set up and accessorize using all of the 40 pins. That's why we now carry the Assembled Adafruit Pi T-Cobbler Plus - Breakout + Cable for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
