# Fritzing sketch d2t3-5 (saved by Fritzing 0.9.3b)
breadboards: 1

parts:
  Part1 = Adafruit T-Cobbler Plus [part_number="Adafruit #1989 and #2028"]
  R1 = Resistor [tolerance=±1% resistance=56 package=THT]
  R2 = Resistor [tolerance=±5% resistance=10k package=THT]
  LED1 = LED - 5mm [color="Red (633nm)" package="5 mm [THT]"]
  LED2 = LED - 5mm [color="Yellow (585nm)" package="5 mm [THT]"]
  LED3 = LED - 5mm [color="Green (555nm)" package="5 mm [THT]"]
  LED4 = LED - 5mm [color="Red (633nm)" package="5 mm [THT]"]
  LED5 = LED - 5mm [color="Green (555nm)" package="5 mm [THT]"]
  S1 = Pushbutton [package="[THT]"]
  R3 = Resistor [tolerance=±1% resistance=56 package=THT]
  R4 = Resistor [tolerance=±1% resistance=56 package=THT]
  R5 = Resistor [tolerance=±1% resistance=56 package=THT]
  R6 = Resistor [tolerance=±1% resistance=56 package=THT]
  LED6 = LED - 5mm [color="Yellow (585nm)" package="5 mm [THT]"]
  R7 = Resistor [tolerance=±1% resistance=56 package=THT]
  J1 = Infrared Proximity Sensor

nets:
  N1: Part1.GPIO4, R1.Pin_1
  GND: Part1.GND, R2.Pin_0, LED1.cathode, LED2.cathode, LED3.cathode, LED4.cathode, LED5.cathode, LED6.cathode, J1.GND
  N2: Part1.GPIO5, R3.Pin_1
  N3: Part1.GPIO6, R4.Pin_1
  N4: Part1.GPIO13, J1.Vout
  N5: Part1.GPIO26, R2.Pin_1, S1.Pin_1, S1.Pin_2
  +5V: Part1.+5V, S1.Pin_3, S1.Pin_4, J1.Vcc
  N6: Part1.GPIO16, R7.Pin_1
  N7: Part1.GPIO20, R6.Pin_1
  N8: Part1.GPIO21, R5.Pin_1
  N9: R1.Pin_0, LED3.anode
  N10: LED1.anode, R4.Pin_0
  N11: LED2.anode, R3.Pin_0
  N12: LED4.anode, R5.Pin_0
  N13: LED5.anode, R6.Pin_0
  N14: LED6.anode, R7.Pin_0

custom parts:
  Adafruit T-Cobbler Plus: The Raspberry Pi has landed on the Maker World like a 40-GPIO pinned, quad-USB ported, credit card sized bomb of DIY joy. And while you can use most of our great Model B accessories by hooking up our downgrade cable, its probably a good time to upgrade your set up and accessorize using all of the 40 pins. That's why we now carry the Assembled Adafruit Pi T-Cobbler Plus - Breakout + Cable for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
